# Fritzing sketch binary to leds (saved by Fritzing 0.9.9b)
breadboards: 1

parts:
  Part6 = Arduino Uno (Rev3)
  Part7 = Arduino Uno (Rev3)
  M5 = Niren can bus module [package=THT]
  M6 = Niren can bus module [package=THT]
  R1 = Resistor [tolerance=±5% resistance=220 package="0402 [SMD]"]
  R2 = Resistor [tolerance=±5% resistance=220 package="0402 [SMD]"]
  R3 = Resistor [tolerance=±5% resistance=220 package="0402 [SMD]"]
  R4 = Resistor [tolerance=±5% resistance=220 package="0402 [SMD]"]
  LED1 = LED - 5mm [color="Red (633nm)" package="5 mm [THT]"]
  LED2 = LED - 5mm [color="Red (633nm)" package="5 mm [THT]"]
  LED3 = LED - 5mm [color="Red (633nm)" package="5 mm [THT]"]
  LED4 = LED - 5mm [color="Red (633nm)" package="5 mm [THT]"]

nets:
  N1: Part6.D10_PWM/SS, M6.pin3
  N2: Part6.D11_PWM/MOSI, M6.pin5
  N3: Part6.D12/MISO, M6.pin4
  N4: Part6.D13/SCK, M6.pin6
  N5: Part6.D2, M6.pin7
  N6: Part6.5V, M6.pin1
  N7: Part6.GND, M6.pin2
  N8: Part7.D10_PWM/SS, M5.pin3
  N9: Part7.D11_PWM/MOSI, M5.pin5
  N10: Part7.D12/MISO, M5.pin4
  N11: Part7.D13/SCK, M5.pin6
  N12: Part7.D2, M5.pin7
  N13: Part7.D4, R4.Pin_1, LED4.cathode, LED4.anode
  N14: Part7.D5_PWM, R3.Pin_1, LED3.cathode, LED3.anode
  N15: Part7.D6_PWM, R2.Pin_1, LED2.cathode, LED2.anode
  N16: Part7.D7, R1.Pin_1, LED1.cathode, LED1.anode
  N17: Part7.5V, M5.pin1
  N18: Part7.GND, M5.pin2, R1.Pin_0, R2.Pin_0, R3.Pin_0, R4.Pin_0
  N19: M5.pin10, M6.pin10
  N20: M5.pin11, M6.pin11

custom parts:
  Niren can bus module: Niren can bus module availabe on ebay and others. Pcb view assumes that you unsolder the 7 pin header and resolder it on the bottom of the module to connect to the pcb. The two jumpers and the can bus connector remain on the top of the board and don't appear in pcb view.
