# Fritzing sketch door monitoring system (saved by Fritzing 0.9.9b)
breadboards: 1

parts:
  Part3 = Arduino Uno (Rev3)
  M3 = Niren can bus module [package=THT]
  Part4 = Arduino Uno (Rev3)
  M4 = Niren can bus module [package=THT]
  Part5 = RFID-RC522-v2

nets:
  N1: Part3.D8, Part5.SDA
  N2: Part3.D9_PWM, Part5.RST
  N3: Part3.D10_PWM/SS, M3.pin3
  N4: Part3.D11_PWM/MOSI, M3.pin5, Part5.SCK
  N5: Part3.D12/MISO, M3.pin4, Part5.MISO
  N6: Part3.D13/SCK, M3.pin6, Part5.MOSI
  N7: Part3.D2, M3.pin7
  3V3: Part3.3V3, Part5.3.3V
  N8: Part3.5V, M3.pin1
  GND: Part3.GND, M3.pin2, Part5.GND
  N9: M3.pin10, M4.pin10
  N10: M3.pin11, M4.pin11
  N11: Part4.D10_PWM/SS, M4.pin3
  N12: Part4.D11_PWM/MOSI, M4.pin5
  N13: Part4.D12/MISO, M4.pin4
  N14: Part4.D13/SCK, M4.pin6
  N15: Part4.D2, M4.pin7
  N16: Part4.5V, M4.pin1
  N17: Part4.GND, M4.pin2

custom parts:
  Niren can bus module: Niren can bus module availabe on ebay and others. Pcb view assumes that you unsolder the 7 pin header and resolder it on the bottom of the module to connect to the pcb. The two jumpers and the can bus connector remain on the top of the board and don't appear in pcb view.
  RFID-RC522-v2: A simple China made RFID-RC522 Reader; do check the pin labels, as this is a MFRC522 based clone.
